# Fritzing sketch Sleep_coach_tiny_schematic_Rotary_Encoder_small (saved by Fritzing 0.8.7b)
circuit board: 4.99613cm x 3.78567cm
breadboards: 1

parts:
  U1 = attiny85 [package=dip]
  VCC1 = Battery
  C1 = Electrolytic Capacitor [capacitance=1µF package="0405 [SMD, electrolytic]"]
  LED1 = LED - 5mm [color="Blue (525nm)" package="5 mm [THT]"]
  LED2 = LED - 5mm [color="Blue (525nm)" package="5 mm [THT]"]
  LED3 = LED - 5mm [color="Blue (525nm)" package="5 mm [THT]"]
  LED4 = LED - 5mm [color="Blue (525nm)" package="5 mm [THT]"]
  C2 = Electrolytic Capacitor [capacitance=1µF package="100 mil [THT, electrolytic]"]
  R3 = Resistor [tolerance=±5% resistance=10k package=THT]
  R4 = Resistor [tolerance=±5% resistance=10k package=THT]
  R5 = Resistor [tolerance=±5% resistance=220 package=THT]
  R7 = Resistor [tolerance=±5% resistance=10k package="0603 [SMD]"]
  R6 = Resistor [tolerance=±5% resistance=10k package="0603 [SMD]"]
  R8 = Resistor [tolerance=±5% resistance=220 package="0603 [SMD]"]
  ENCODER1 = Rotary Encoder with Knob

nets:
  N1: U1.Pin_2, R3.Pin_1, R7.Pin_1, ENCODER1.no_name_yet#3
  N2: U1.Pin_3, R4.Pin_1, R6.Pin_1, ENCODER1.no_name_yet#1
  N3: U1.Pin_4, VCC1.-, C1.+, LED1.cathode, LED2.cathode, LED3.cathode, LED4.cathode, C2.-, R5.Pin_1, R8.Pin_1, ENCODER1.no_name_yet#2
  N4: U1.Pin_5, LED1.anode, LED2.anode, LED3.anode, LED4.anode
  N5: U1.Pin_6, R5.Pin_0, R8.Pin_0, ENCODER1.no_name_yet#5
  N6: U1.Pin_8, VCC1.+, C1.-, C2.+, R3.Pin_0, R4.Pin_0, R7.Pin_0, R6.Pin_0, ENCODER1.no_name_yet#4

notes:
  Sleep Sensei
  getsleepsensei.com
  github.com/jerwil/SleepCoach

custom parts:
  Rotary Encoder with Knob: Rotary Encoder with 1/4" Shaft and Knob
