# Fritzing sketch Sleep_coach_tiny_schematic_battery_SMD_Quote_PotSwap_CapOptions (saved by Fritzing 0.8.7b)
circuit board: 4.9cm x 3.81cm
breadboards: 1

parts:
  S1 = Pushbutton [package="[THT]"]
  J1 = female pin header, 1 pin [form="♀ (female)"]
  J2 = female pin header, 1 pin [form="♀ (female)"]
  J3 = female pin header, 1 pin [form="♀ (female)"]
  U1 = attiny85 [package=dip]
  VCC1 = Battery
  R1 = Resistor [tolerance=±5% resistance=220 package="0603 [SMD]"]
  C1 = Electrolytic Capacitor [capacitance=1µF package="0405 [SMD, electrolytic]"]
  LED1 = LED - 5mm [color="Blue (525nm)" package="5 mm [THT]"]
  LED2 = LED - 5mm [color="Blue (525nm)" package="5 mm [THT]"]
  LED3 = LED - 5mm [color="Blue (525nm)" package="5 mm [THT]"]
  LED4 = LED - 5mm [color="Blue (525nm)" package="5 mm [THT]"]
  C2 = Electrolytic Capacitor [capacitance=1µF package="100 mil [THT, electrolytic]"]
  R2 = Resistor [tolerance=±5% resistance=220 package=THT]

nets:
  N1: S1.Pin_1, S1.Pin_2, U1.Pin_6, R1.Pin_1, R2.Pin_1
  N2: S1.Pin_3, S1.Pin_4, J1.pin1, U1.Pin_8, VCC1.+, C1.-, C2.-
  N3: J2.pin1, U1.Pin_4, VCC1.-, R1.Pin_0, C1.+, LED1.cathode, LED2.cathode, LED3.cathode, LED4.cathode, C2.+, R2.Pin_0
  N4: J3.pin1, U1.Pin_2
  N5: U1.Pin_5, LED1.anode, LED2.anode, LED3.anode, LED4.anode

notes:
  Sleep Sensei
  getsleepsensei.com
  github.com/jerwil/SleepCoach
